# Fritzing sketch boitier_recepteur (saved by Fritzing 0.8.3b)
breadboards: 1

parts:
  Composants1 = Arduino Uno (Rev3)
  D1 = Rectifier Diode [part_number=1N4001 package="300 mil [THT]"]
  D2 = Rectifier Diode [part_number=1N4001 package="300 mil [THT]"]
  S1 = Pushbutton [package=THT]
  S2 = Pushbutton [package=THT]
  R1 = Resistor [tolerance=±5% resistance=10k package=THT]
  R2 = Resistor [tolerance=±5% resistance=10k package=THT]
  U1 = XBee
  R3 = Resistor [tolerance=±5% resistance=10k package=THT]
  R4 = Resistor [tolerance=±5% resistance=15k package=THT]
  VCC1 = Battery block 9V  # not connected

nets:
  GND: Composants1.GND, S1.leg0, S2.leg0, U1.GND, R4.Pin_1
  N1: Composants1.D0/RX, U1.pin2
  N2: Composants1.D1/TX, R3.Pin_1
  N3: Composants1.D2, D1.anode, D2.anode
  N4: Composants1.D3_PWM, D2.cathode, S1.leg1, R1.Pin_1
  N5: Composants1.D4, D1.cathode, S2.leg1, R2.Pin_1
  3V3: Composants1.3V3, U1.VCC
  N6: Composants1.5V, R1.Pin_0, R2.Pin_0
  N7: U1.pin3, R3.Pin_0, R4.Pin_0
