# Fritzing sketch interrupts (saved by Fritzing 0.8.3b)
breadboards: 1

parts:
  Composants1 = Arduino Uno (Rev3)
  S1 = Pushbutton [package=THT]
  S2 = Pushbutton [package=THT]
  R1 = Resistor [tolerance=±5% resistance=10k package=THT]
  R2 = Resistor [tolerance=±5% resistance=10k package=THT]
  D1 = Rectifier Diode [part_number=1N4001 package="300 mil [THT]"]
  D2 = Rectifier Diode [part_number=1N4001 package="300 mil [THT]"]

nets:
  N1: Composants1.GND, Composants1.D3_PWM, Composants1.D4, S1.leg0, S2.leg0, D1.cathode, D2.cathode
  N2: Composants1.D2, D1.anode, D2.anode
  N3: Composants1.5V, R1.Pin_0, R2.Pin_0
  N4: S1.leg1, R1.Pin_1
  N5: S2.leg1, R2.Pin_1
