# Fritzing sketch xbee_arduino (saved by Fritzing 0.8.3b)

parts:
  Arduino = Arduino Uno (Rev3)
  XBee = XBee
  R1 = Resistor [tolerance=±5% resistance=10k package=THT]
  R2 = Resistor [tolerance=±5% resistance=15k package=THT]

nets (from the breadboard view):
  GND: Arduino.GND, XBee.GND, R2.Pin_1
  N1: Arduino.D0/RX, XBee.pin2
  N2: Arduino.D1/TX, R1.Pin_0
  3V3: Arduino.3V3, XBee.VCC
  N3: XBee.pin3, R1.Pin_1, R2.Pin_0

notes:
  Pont diviseur :
  > Tension d'entrée : 5v
  > Tension de sortie : 3v
  Calcul :
  5 * (15000/(10000+15000)) = 3
